// Logisim project stage3.circ.circ as structural Verilog: 3 circuits, main circuit main
module main (
);

  wire button_1_out, button_3_out, clock_1_out, stage_2_1_and1, stage_2_1_and2, stage_2_1_and3, t_ff_1_q;
  wire [3:0] stage_2_1_led, stage_3_1_out_6;

  Button button_1 (.out(button_1_out));
  Clock clock_1 (.out(clock_1_out));
  Button button_2 ();  // open: out
  T_Flip_Flop t_ff_1 (.T(button_1_out), .clk(button_1_out), .Q(t_ff_1_q), .reset(button_3_out));  // open: Qn, preset
  Button button_3 (.out(button_3_out));
  Stage_2 stage_2_1 (
    .Reset(button_3_out), .Q(t_ff_1_q), .CLK(clock_1_out), .And1(stage_2_1_and1), .Led(stage_2_1_led),
    .And2(stage_2_1_and2), .And3(stage_2_1_and3));
  Stage_3 stage_3_1 (
    .And2(stage_2_1_and2), .And3(stage_2_1_and3), .And1(stage_2_1_and1), .CLK(clock_1_out),
    .Reset2(button_3_out), .out_6(stage_3_1_out_6));
  Hex_Digit_Display hex_digit_display_1 ();  // open: value, dp
  Hex_Digit_Display hex_digit_display_2 ();  // open: value, dp
  Hex_Digit_Display hex_digit_display_3 (.value(stage_3_1_out_6));  // open: dp
  Hex_Digit_Display hex_digit_display_4 (.value(stage_2_1_led));  // open: dp
  Hex_Digit_Display hex_digit_display_5 ();  // open: value, dp
  Hex_Digit_Display hex_digit_display_6 ();  // open: value, dp
  Hex_Digit_Display hex_digit_display_7 ();  // open: value, dp
  Hex_Digit_Display hex_digit_display_8 ();  // open: value, dp

  // Notes on the sheet:
  //   Start / Stop
  //   Split
  //   Reset
  //   Stopwatch Interface
  //   Minutes
  //   Elapsed Time
  //   Seconds
  //   :
  //   Minutes
  //   Split Time
  //   :
  //   Seconds
endmodule

module Stage_2 (
  input  Reset,
  input  Q,
  input  CLK,
  output And1,
  output [3:0] Led,
  output And2,
  output And3
);

  wire and_1_out, and_2_out, and_3_out, and_4_out, and_5_out, j_k_ff_1_q, j_k_ff_3_q, or_1_out;

  and and_1 (and_1_out, Q, CLK);
  J_K_Flip_Flop j_k_ff_1 (.J(Q), .K(Q), .clk(CLK), .Q(j_k_ff_1_q), .reset(or_1_out));  // open: Qn, preset
  D_Flip_Flop d_ff_1 (.D(j_k_ff_1_q), .clk(and_1_out), .Q(Led[0]), .reset(Reset));  // open: Qn, preset
  and and_2 (and_2_out, Q, j_k_ff_1_q);
  J_K_Flip_Flop j_k_ff_2 (.J(and_2_out), .K(and_2_out), .clk(CLK), .Q(And2), .reset(or_1_out));  // open: Qn, preset
  D_Flip_Flop d_ff_2 (.D(And2), .clk(and_1_out), .Q(Led[1]), .reset(Reset));  // open: Qn, preset
  and and_3 (and_3_out, and_2_out, And2);
  J_K_Flip_Flop j_k_ff_3 (
    .J(and_3_out), .K(and_3_out), .clk(CLK), .Q(j_k_ff_3_q), .reset(or_1_out));  // open: Qn, preset
  D_Flip_Flop d_ff_3 (.D(j_k_ff_3_q), .clk(and_1_out), .Q(Led[2]), .reset(Reset));  // open: Qn, preset
  and and_4 (and_4_out, and_3_out, j_k_ff_3_q);
  J_K_Flip_Flop j_k_ff_4 (.J(and_4_out), .K(and_4_out), .clk(CLK), .Q(And3), .reset(or_1_out));  // open: Qn, preset
  D_Flip_Flop d_ff_4 (.D(And3), .clk(and_1_out), .Q(Led[3]), .reset(Reset));  // open: Qn, preset
  and and_5 (and_5_out, And2, And3);
  or or_1 (or_1_out, and_5_out, Reset);

  assign And1 = Q;

  // Notes on the sheet:
  //   Stopwatch Interface
endmodule

module Stage_3 (
  input  And2,
  input  And3,
  input  And1,
  input  CLK,
  input  Reset2,
  output [3:0] out_6
);

  wire and_1_out, and_2_out, and_3_out, and_4_out, j_k_ff_1_q, j_k_ff_2_q, j_k_ff_3_q, or_1_out;

  and and_1 (and_1_out, And1, CLK);
  and and_2 (and_2_out, And2, And3);
  J_K_Flip_Flop j_k_ff_1 (
    .J(and_2_out), .K(and_2_out), .clk(and_2_out), .Q(j_k_ff_1_q), .reset(or_1_out));  // open: Qn, preset
  J_K_Flip_Flop j_k_ff_2 (
    .J(j_k_ff_1_q), .K(j_k_ff_1_q), .clk(and_2_out), .Q(j_k_ff_2_q), .reset(or_1_out));  // open: Qn, preset
  D_Flip_Flop d_ff_1 (.D(j_k_ff_1_q), .clk(and_1_out), .Q(out_6[0]), .reset(Reset2));  // open: Qn, preset
  and and_3 (and_3_out, j_k_ff_1_q, j_k_ff_2_q);
  J_K_Flip_Flop j_k_ff_3 (
    .J(and_3_out), .K(and_3_out), .clk(and_2_out), .Q(j_k_ff_3_q), .reset(or_1_out));  // open: Qn, preset
  D_Flip_Flop d_ff_2 (.D(j_k_ff_2_q), .clk(and_1_out), .Q(out_6[1]), .reset(Reset2));  // open: Qn, preset
  and and_4 (and_4_out, j_k_ff_2_q, j_k_ff_3_q);
  D_Flip_Flop d_ff_3 (.D(j_k_ff_3_q), .clk(and_1_out), .Q(out_6[2]), .reset(Reset2));  // open: Qn, preset
  or or_1 (or_1_out, and_4_out, Reset2);

  assign out_6[3] = 1'b0;
endmodule
