// Logisim project stage6.circ.circ as structural Verilog: 6 circuits, main circuit main
module main (
);

  wire button_1_out, button_2_out, button_3_out, clock_1_out, stage5a_1_bit01, stage5a_1_bit02,
       stage5a_1_bit03, stage5a_1_bit04, stage5a_2_bit01, stage5a_2_bit02, stage5a_2_bit03, stage5a_2_bit04,
       stage5a_3_bit01, stage5a_3_bit02, stage5a_3_bit03, stage5a_3_bit04, stage5a_4_bit01, stage5a_4_bit02,
       stage5a_4_bit03, stage5a_4_bit04, stage5a_5_bit01, stage5a_5_bit02, stage5a_5_bit03, stage5a_5_bit04,
       stage5a_6_bit01, stage5a_6_bit02, stage5a_6_bit03, stage5a_6_bit04, stage5a_7_bit01, stage5a_7_bit02,
       stage5a_7_bit03, stage5a_7_bit04, stage5a_8_bit01, stage5a_8_bit02, stage5a_8_bit03, stage5a_8_bit04,
       stage5a_9_bit01, stage5a_9_bit02, stage5a_9_bit03, stage5a_9_bit04, stage5a_10_bit01,
       stage5a_10_bit02, stage5a_10_bit03, stage5a_10_bit04, stage5a_11_bit01, stage5a_11_bit02,
       stage5a_11_bit03, stage5a_11_bit04, stage5a_12_bit01, stage5a_12_bit02, stage5a_12_bit03,
       stage5a_12_bit04, stage_2_1_and1, stage_2_1_and2, stage_2_1_and3, stage_2_1_bit1, stage_2_1_bit2,
       stage_2_1_bit3, stage_2_1_bit4, stage_3_1_bit1, stage_3_1_bit2, stage_3_1_bit3, stage_3_1_d1,
       stage_3_1_d2, stage_4_1_bit1, stage_4_1_bit2, stage_4_1_bit3, stage_4_1_bit4, stage_4_1_d01,
       stage_4_1_d02, stage_4_1_rset, stage_4_2_bit1, stage_4_2_bit2, stage_4_2_bit3, stage_4_2_bit4,
       stage_5b_1_bit01, stage_5b_1_bit02, stage_5b_1_bit03, stage_5b_2_bit01, stage_5b_2_bit02,
       stage_5b_2_bit03, stage_5b_3_bit01, stage_5b_3_bit02, stage_5b_3_bit03, stage_5b_4_bit01,
       stage_5b_4_bit02, stage_5b_4_bit03, t_ff_1_q;
  wire [3:0] stage5a_1_led, stage5a_2_led, stage5a_3_led, stage5a_4_led, stage5a_5_led, stage5a_6_led,
       stage5a_7_led, stage5a_8_led, stage5a_9_led, stage5a_10_led, stage5a_11_led, stage5a_12_led,
       stage5a_13_led, stage5a_14_led, stage5a_15_led, stage_2_1_led, stage_3_1_led, stage_4_1_led,
       stage_4_2_led, stage_5b_1_led, stage_5b_2_led, stage_5b_3_led, stage_5b_4_led, stage_5b_5_led;

  Button button_1 (.out(button_1_out));
  Button button_2 (.out(button_2_out));
  T_Flip_Flop t_ff_1 (.T(button_2_out), .clk(button_2_out), .Q(t_ff_1_q), .reset(button_3_out));  // open: Qn, preset
  Clock clock_1 (.out(clock_1_out));
  Button button_3 (.out(button_3_out));
  Stage_2 stage_2_1 (
    .Reset(button_3_out), .Q(t_ff_1_q), .CLK(clock_1_out), .And1(stage_2_1_and1), .Led(stage_2_1_led),
    .And2(stage_2_1_and2), .And3(stage_2_1_and3), .Bit1(stage_2_1_bit1), .Bit2(stage_2_1_bit2),
    .Bit3(stage_2_1_bit3), .Bit4(stage_2_1_bit4));
  Stage_3 stage_3_1 (
    .And2(stage_2_1_and2), .And3(stage_2_1_and3), .And1(stage_2_1_and1), .CLK(clock_1_out),
    .Reset(button_3_out), .Led(stage_3_1_led), .Bit1(stage_3_1_bit1), .Bit2(stage_3_1_bit2),
    .Bit3(stage_3_1_bit3), .D1(stage_3_1_d1), .D2(stage_3_1_d2));
  Stage_4 stage_4_1 (
    .D1(stage_3_1_d1), .D2(stage_3_1_d2), .Reset(button_3_out), .Stop(t_ff_1_q), .CLK(clock_1_out),
    .Rset(stage_4_1_rset), .Led(stage_4_1_led), .Bit1(stage_4_1_bit1), .Bit2(stage_4_1_bit2),
    .Bit3(stage_4_1_bit3), .Bit4(stage_4_1_bit4), .D01(stage_4_1_d01), .D02(stage_4_1_d02));
  Stage_4 stage_4_2 (
    .D1(stage_4_1_d01), .D2(stage_4_1_d02), .Reset(stage_4_1_rset), .Stop(t_ff_1_q), .CLK(clock_1_out),
    .Led(stage_4_2_led), .Bit1(stage_4_2_bit1), .Bit2(stage_4_2_bit2), .Bit3(stage_4_2_bit3),
    .Bit4(stage_4_2_bit4));  // open: Rset, D01, D02
  Hex_Digit_Display hex_digit_display_1 (.value(stage_4_2_led));  // open: dp
  Hex_Digit_Display hex_digit_display_2 (.value(stage_4_1_led));  // open: dp
  Hex_Digit_Display hex_digit_display_3 (.value(stage_3_1_led));  // open: dp
  Hex_Digit_Display hex_digit_display_4 (.value(stage_2_1_led));  // open: dp
  Hex_Digit_Display hex_digit_display_5 (.value(stage5a_3_led));  // open: dp
  Hex_Digit_Display hex_digit_display_6 (.value(stage5a_2_led));  // open: dp
  Stage5a stage5a_1 (
    .Bit1(stage_2_1_bit1), .Bit2(stage_2_1_bit2), .Bit3(stage_2_1_bit3), .Bit4(stage_2_1_bit4),
    .Reset(button_3_out), .Split(button_1_out), .Led(stage5a_1_led), .Bit01(stage5a_1_bit01),
    .Bit02(stage5a_1_bit02), .Bit03(stage5a_1_bit03), .Bit04(stage5a_1_bit04));
  Stage_5b stage_5b_1 (
    .Bit1(stage_3_1_bit1), .Bit2(stage_3_1_bit2), .Bit3(stage_3_1_bit3), .Split(button_1_out),
    .Reset(button_3_out), .Led(stage_5b_1_led), .Bit01(stage_5b_1_bit01), .Bit02(stage_5b_1_bit02),
    .Bit03(stage_5b_1_bit03));
  Stage5a stage5a_2 (
    .Bit1(stage_4_1_bit1), .Bit2(stage_4_1_bit2), .Bit3(stage_4_1_bit3), .Bit4(stage_4_1_bit4),
    .Reset(button_3_out), .Split(button_1_out), .Led(stage5a_2_led), .Bit01(stage5a_2_bit01),
    .Bit02(stage5a_2_bit02), .Bit03(stage5a_2_bit03), .Bit04(stage5a_2_bit04));
  Stage5a stage5a_3 (
    .Bit1(stage_4_2_bit1), .Bit2(stage_4_2_bit2), .Bit3(stage_4_2_bit3), .Bit4(stage_4_2_bit4),
    .Reset(button_3_out), .Split(button_1_out), .Led(stage5a_3_led), .Bit01(stage5a_3_bit01),
    .Bit02(stage5a_3_bit02), .Bit03(stage5a_3_bit03), .Bit04(stage5a_3_bit04));
  Hex_Digit_Display hex_digit_display_7 (.value(stage_5b_1_led));  // open: dp
  Hex_Digit_Display hex_digit_display_8 (.value(stage5a_1_led));  // open: dp
  Hex_Digit_Display hex_digit_display_9 (.value(stage5a_6_led));  // open: dp
  Hex_Digit_Display hex_digit_display_10 (.value(stage5a_5_led));  // open: dp
  Stage5a stage5a_4 (
    .Bit1(stage5a_1_bit01), .Bit2(stage5a_1_bit02), .Bit3(stage5a_1_bit03), .Bit4(stage5a_1_bit04),
    .Reset(button_3_out), .Split(button_1_out), .Led(stage5a_4_led), .Bit01(stage5a_4_bit01),
    .Bit02(stage5a_4_bit02), .Bit03(stage5a_4_bit03), .Bit04(stage5a_4_bit04));
  Stage_5b stage_5b_2 (
    .Bit1(stage_5b_1_bit01), .Bit2(stage_5b_1_bit02), .Bit3(stage_5b_1_bit03), .Split(button_1_out),
    .Reset(button_3_out), .Led(stage_5b_2_led), .Bit01(stage_5b_2_bit01), .Bit02(stage_5b_2_bit02),
    .Bit03(stage_5b_2_bit03));
  Stage5a stage5a_5 (
    .Bit1(stage5a_2_bit01), .Bit2(stage5a_2_bit02), .Bit3(stage5a_2_bit03), .Bit4(stage5a_2_bit04),
    .Reset(button_3_out), .Split(button_1_out), .Led(stage5a_5_led), .Bit01(stage5a_5_bit01),
    .Bit02(stage5a_5_bit02), .Bit03(stage5a_5_bit03), .Bit04(stage5a_5_bit04));
  Stage5a stage5a_6 (
    .Bit1(stage5a_3_bit01), .Bit2(stage5a_3_bit02), .Bit3(stage5a_3_bit03), .Bit4(stage5a_3_bit04),
    .Reset(button_3_out), .Split(button_1_out), .Led(stage5a_6_led), .Bit01(stage5a_6_bit01),
    .Bit02(stage5a_6_bit02), .Bit03(stage5a_6_bit03), .Bit04(stage5a_6_bit04));
  Hex_Digit_Display hex_digit_display_11 (.value(stage_5b_2_led));  // open: dp
  Hex_Digit_Display hex_digit_display_12 (.value(stage5a_4_led));  // open: dp
  Hex_Digit_Display hex_digit_display_13 (.value(stage5a_9_led));  // open: dp
  Hex_Digit_Display hex_digit_display_14 (.value(stage5a_8_led));  // open: dp
  Stage5a stage5a_7 (
    .Bit1(stage5a_4_bit01), .Bit2(stage5a_4_bit02), .Bit3(stage5a_4_bit03), .Bit4(stage5a_4_bit04),
    .Reset(button_3_out), .Split(button_1_out), .Led(stage5a_7_led), .Bit01(stage5a_7_bit01),
    .Bit02(stage5a_7_bit02), .Bit03(stage5a_7_bit03), .Bit04(stage5a_7_bit04));
  Stage_5b stage_5b_3 (
    .Bit1(stage_5b_2_bit01), .Bit2(stage_5b_2_bit02), .Bit3(stage_5b_2_bit03), .Split(button_1_out),
    .Reset(button_3_out), .Led(stage_5b_3_led), .Bit01(stage_5b_3_bit01), .Bit02(stage_5b_3_bit02),
    .Bit03(stage_5b_3_bit03));
  Stage5a stage5a_8 (
    .Bit1(stage5a_5_bit01), .Bit2(stage5a_5_bit02), .Bit3(stage5a_5_bit03), .Bit4(stage5a_5_bit04),
    .Reset(button_3_out), .Split(button_1_out), .Led(stage5a_8_led), .Bit01(stage5a_8_bit01),
    .Bit02(stage5a_8_bit02), .Bit03(stage5a_8_bit03), .Bit04(stage5a_8_bit04));
  Stage5a stage5a_9 (
    .Bit1(stage5a_6_bit01), .Bit2(stage5a_6_bit02), .Bit3(stage5a_6_bit03), .Bit4(stage5a_6_bit04),
    .Reset(button_3_out), .Split(button_1_out), .Led(stage5a_9_led), .Bit01(stage5a_9_bit01),
    .Bit02(stage5a_9_bit02), .Bit03(stage5a_9_bit03), .Bit04(stage5a_9_bit04));
  Hex_Digit_Display hex_digit_display_15 (.value(stage_5b_3_led));  // open: dp
  Hex_Digit_Display hex_digit_display_16 (.value(stage5a_7_led));  // open: dp
  Hex_Digit_Display hex_digit_display_17 (.value(stage5a_12_led));  // open: dp
  Stage5a stage5a_10 (
    .Bit1(stage5a_7_bit01), .Bit2(stage5a_7_bit02), .Bit3(stage5a_7_bit03), .Bit4(stage5a_7_bit04),
    .Reset(button_3_out), .Split(button_1_out), .Led(stage5a_10_led), .Bit01(stage5a_10_bit01),
    .Bit02(stage5a_10_bit02), .Bit03(stage5a_10_bit03), .Bit04(stage5a_10_bit04));
  Stage_5b stage_5b_4 (
    .Bit1(stage_5b_3_bit01), .Bit2(stage_5b_3_bit02), .Bit3(stage_5b_3_bit03), .Split(button_1_out),
    .Reset(button_3_out), .Led(stage_5b_4_led), .Bit01(stage_5b_4_bit01), .Bit02(stage_5b_4_bit02),
    .Bit03(stage_5b_4_bit03));
  Stage5a stage5a_11 (
    .Bit1(stage5a_8_bit01), .Bit2(stage5a_8_bit02), .Bit3(stage5a_8_bit03), .Bit4(stage5a_8_bit04),
    .Reset(button_3_out), .Split(button_1_out), .Led(stage5a_11_led), .Bit01(stage5a_11_bit01),
    .Bit02(stage5a_11_bit02), .Bit03(stage5a_11_bit03), .Bit04(stage5a_11_bit04));
  Stage5a stage5a_12 (
    .Bit1(stage5a_9_bit01), .Bit2(stage5a_9_bit02), .Bit3(stage5a_9_bit03), .Bit4(stage5a_9_bit04),
    .Reset(button_3_out), .Split(button_1_out), .Led(stage5a_12_led), .Bit01(stage5a_12_bit01),
    .Bit02(stage5a_12_bit02), .Bit03(stage5a_12_bit03), .Bit04(stage5a_12_bit04));
  Hex_Digit_Display hex_digit_display_18 (.value(stage5a_11_led));  // open: dp
  Hex_Digit_Display hex_digit_display_19 (.value(stage_5b_4_led));  // open: dp
  Hex_Digit_Display hex_digit_display_20 (.value(stage5a_10_led));  // open: dp
  Hex_Digit_Display hex_digit_display_21 (.value(stage5a_15_led));  // open: dp
  Stage5a stage5a_13 (
    .Bit1(stage5a_10_bit01), .Bit2(stage5a_10_bit02), .Bit3(stage5a_10_bit03), .Bit4(stage5a_10_bit04),
    .Reset(button_3_out), .Split(button_1_out), .Led(stage5a_13_led));  // open: Bit01, Bit02, Bit03, Bit04
  Stage_5b stage_5b_5 (
    .Bit1(stage_5b_4_bit01), .Bit2(stage_5b_4_bit02), .Bit3(stage_5b_4_bit03), .Split(button_1_out),
    .Reset(button_3_out), .Led(stage_5b_5_led));  // open: Bit01, Bit02, Bit03
  Stage5a stage5a_14 (
    .Bit1(stage5a_11_bit01), .Bit2(stage5a_11_bit02), .Bit3(stage5a_11_bit03), .Bit4(stage5a_11_bit04),
    .Reset(button_3_out), .Split(button_1_out), .Led(stage5a_14_led));  // open: Bit01, Bit02, Bit03, Bit04
  Stage5a stage5a_15 (
    .Bit1(stage5a_12_bit01), .Bit2(stage5a_12_bit02), .Bit3(stage5a_12_bit03), .Bit4(stage5a_12_bit04),
    .Reset(button_3_out), .Split(button_1_out), .Led(stage5a_15_led));  // open: Bit01, Bit02, Bit03, Bit04
  Hex_Digit_Display hex_digit_display_22 (.value(stage5a_14_led));  // open: dp
  Hex_Digit_Display hex_digit_display_23 (.value(stage_5b_5_led));  // open: dp
  Hex_Digit_Display hex_digit_display_24 (.value(stage5a_13_led));  // open: dp

  // Notes on the sheet:
  //   Split
  //   Stopwatch Interface
  //   Start / Stop
  //   Reset
  //   Minutes
  //   Elapsed Time
  //   :
  //   Seconds
  //   Minutes
  //   Split Time 1
  //   Seconds
  //   :
  //   Minutes
  //   Split Time 2
  //   :
  //   Seconds
  //   Minutes
  //   Split Time 3
  //   :
  //   Seconds
  //   Minutes
  //   Split Time 4
  //   :
  //   Seconds
  //   Minutes
  //   Split Time 5
  //   :
  //   Seconds
endmodule

module Stage_2 (
  input  Reset,
  input  Q,
  input  CLK,
  output And1,
  output [3:0] Led,
  output And2,
  output And3,
  output Bit1,
  output Bit2,
  output Bit3,
  output Bit4
);

  wire and_1_out, and_2_out, and_3_out, and_4_out, and_5_out, j_k_ff_1_q, j_k_ff_3_q, or_1_out;

  and and_1 (and_1_out, Q, CLK);
  J_K_Flip_Flop j_k_ff_1 (.J(Q), .K(Q), .clk(CLK), .Q(j_k_ff_1_q), .reset(or_1_out));  // open: Qn, preset
  D_Flip_Flop d_ff_1 (.D(j_k_ff_1_q), .clk(and_1_out), .Q(Bit1), .reset(Reset));  // open: Qn, preset
  and and_2 (and_2_out, Q, j_k_ff_1_q);
  J_K_Flip_Flop j_k_ff_2 (.J(and_2_out), .K(and_2_out), .clk(CLK), .Q(And2), .reset(or_1_out));  // open: Qn, preset
  D_Flip_Flop d_ff_2 (.D(And2), .clk(and_1_out), .Q(Bit2), .reset(Reset));  // open: Qn, preset
  and and_3 (and_3_out, and_2_out, And2);
  J_K_Flip_Flop j_k_ff_3 (
    .J(and_3_out), .K(and_3_out), .clk(CLK), .Q(j_k_ff_3_q), .reset(or_1_out));  // open: Qn, preset
  D_Flip_Flop d_ff_3 (.D(j_k_ff_3_q), .clk(and_1_out), .Q(Bit3), .reset(Reset));  // open: Qn, preset
  and and_4 (and_4_out, and_3_out, j_k_ff_3_q);
  J_K_Flip_Flop j_k_ff_4 (.J(and_4_out), .K(and_4_out), .clk(CLK), .Q(And3), .reset(or_1_out));  // open: Qn, preset
  D_Flip_Flop d_ff_4 (.D(And3), .clk(and_1_out), .Q(Bit4), .reset(Reset));  // open: Qn, preset
  and and_5 (and_5_out, And2, And3);
  or or_1 (or_1_out, and_5_out, Reset);

  assign And1 = Q;
  assign Led = {Bit4, Bit3, Bit2, Bit1};

  // Notes on the sheet:
  //   Stopwatch Interface
endmodule

module Stage_3 (
  input  And2,
  input  And3,
  input  And1,
  input  CLK,
  input  Reset,
  output [3:0] Led,
  output Bit1,
  output Bit2,
  output Bit3,
  output D1,
  output D2
);

  wire and_1_out, and_2_out, and_3_out, and_4_out, j_k_ff_1_q, or_1_out;

  and and_1 (and_1_out, And1, CLK);
  and and_2 (and_2_out, And2, And3);
  J_K_Flip_Flop j_k_ff_1 (
    .J(and_2_out), .K(and_2_out), .clk(and_2_out), .Q(j_k_ff_1_q), .reset(or_1_out));  // open: Qn, preset
  J_K_Flip_Flop j_k_ff_2 (
    .J(j_k_ff_1_q), .K(j_k_ff_1_q), .clk(and_2_out), .Q(D1), .reset(or_1_out));  // open: Qn, preset
  D_Flip_Flop d_ff_1 (.D(j_k_ff_1_q), .clk(and_1_out), .Q(Bit1), .reset(Reset));  // open: Qn, preset
  and and_3 (and_3_out, j_k_ff_1_q, D1);
  J_K_Flip_Flop j_k_ff_3 (.J(and_3_out), .K(and_3_out), .clk(and_2_out), .Q(D2), .reset(or_1_out));  // open: Qn, preset
  D_Flip_Flop d_ff_2 (.D(D1), .clk(and_1_out), .Q(Bit2), .reset(Reset));  // open: Qn, preset
  and and_4 (and_4_out, D1, D2);
  D_Flip_Flop d_ff_3 (.D(D2), .clk(and_1_out), .Q(Bit3), .reset(Reset));  // open: Qn, preset
  or or_1 (or_1_out, and_4_out, Reset);

  assign Led = {1'b0, Bit3, Bit2, Bit1};
endmodule

module Stage_4 (
  input  D1,
  input  D2,
  input  Reset,
  input  Stop,
  input  CLK,
  output Rset,
  output [3:0] Led,
  output Bit1,
  output Bit2,
  output Bit3,
  output Bit4,
  output D01,
  output D02
);

  wire and_1_out, and_2_out, and_3_out, and_4_out, and_5_out, and_6_out, j_k_ff_1_q, j_k_ff_3_q, or_1_out;

  and and_1 (and_1_out, D1, D2);
  and and_2 (and_2_out, Stop, CLK);
  J_K_Flip_Flop j_k_ff_1 (
    .J(and_1_out), .K(and_1_out), .clk(and_1_out), .Q(j_k_ff_1_q), .reset(or_1_out));  // open: Qn, preset
  and and_3 (and_3_out, j_k_ff_1_q, j_k_ff_1_q);
  D_Flip_Flop d_ff_1 (.D(j_k_ff_1_q), .clk(and_2_out), .Q(Bit1), .reset(Reset));  // open: Qn, preset
  J_K_Flip_Flop j_k_ff_2 (
    .J(and_3_out), .K(and_3_out), .clk(and_1_out), .Q(D01), .reset(or_1_out));  // open: Qn, preset
  and and_4 (and_4_out, and_3_out, D01);
  J_K_Flip_Flop j_k_ff_3 (
    .J(and_4_out), .K(and_4_out), .clk(and_1_out), .Q(j_k_ff_3_q), .reset(or_1_out));  // open: Qn, preset
  D_Flip_Flop d_ff_2 (.D(D01), .clk(and_2_out), .Q(Bit2), .reset(Reset));  // open: Qn, preset
  and and_5 (and_5_out, and_4_out, j_k_ff_3_q);
  J_K_Flip_Flop j_k_ff_4 (
    .J(and_5_out), .K(and_5_out), .clk(and_1_out), .Q(D02), .reset(or_1_out));  // open: Qn, preset
  D_Flip_Flop d_ff_3 (.D(j_k_ff_3_q), .clk(and_2_out), .Q(Bit3), .reset(Reset));  // open: Qn, preset
  or or_1 (or_1_out, and_6_out, Reset);
  and and_6 (and_6_out, D02, D01);
  D_Flip_Flop d_ff_4 (.D(D02), .clk(and_2_out), .Q(Bit4), .reset(Reset));  // open: Qn, preset

  assign Led = {Bit4, Bit3, Bit2, Bit1};
  assign Rset = Reset;
endmodule

module Stage5a (
  input  Bit1,
  input  Bit2,
  input  Bit3,
  input  Bit4,
  input  Reset,
  input  Split,
  output [3:0] Led,
  output Bit01,
  output Bit02,
  output Bit03,
  output Bit04
);

  D_Flip_Flop d_ff_1 (.D(Bit1), .clk(Split), .Q(Bit01), .reset(Reset));  // open: Qn, preset
  D_Flip_Flop d_ff_2 (.D(Bit2), .clk(Split), .Q(Bit02), .reset(Reset));  // open: Qn, preset
  D_Flip_Flop d_ff_3 (.D(Bit3), .clk(Split), .Q(Bit03), .reset(Reset));  // open: Qn, preset
  D_Flip_Flop d_ff_4 (.D(Bit4), .clk(Split), .Q(Bit04), .reset(Reset));  // open: Qn, preset

  assign Led = {Bit04, Bit03, Bit02, Bit01};
endmodule

module Stage_5b (
  input  Bit1,
  input  Bit2,
  input  Bit3,
  input  Split,
  input  Reset,
  output [3:0] Led,
  output Bit01,
  output Bit02,
  output Bit03
);

  D_Flip_Flop d_ff_1 (.D(Bit1), .clk(Split), .Q(Bit01), .reset(Reset));  // open: Qn, preset
  D_Flip_Flop d_ff_2 (.D(Bit2), .clk(Split), .Q(Bit02), .reset(Reset));  // open: Qn, preset
  D_Flip_Flop d_ff_3 (.D(Bit3), .clk(Split), .Q(Bit03), .reset(Reset));  // open: Qn, preset

  assign Led = {1'b0, Bit03, Bit02, Bit01};
endmodule
